# Fritzing sketch Schematic_HC_05 (saved by Fritzing 0.9.4)

parts:
  Part1 = Arduino Mega 2560 (Rev3)
  Part2 = Bluetooth HC-05 Macho

nets:
  N1: Part1.D17_PWM/RX2, Part2.TXD
  N2: Part1.D16_PWM/TX2, Part2.RXD
  5V: Part1.5V, Part2.VCC
  GND: Part1.GND, Part2.GND
