# Fritzing sketch Schematic_Lidar_Lite (saved by Fritzing 0.9.4)

parts:
  Part1 = Arduino Mega 2560 (Rev3)
  Part2 = LIDAR-Lite

nets:
  N1: Part1.D15/RX3, Part2.SCL
  N2: Part1.D14/TX3, Part2.SDA
  5V: Part1.5V, Part2.5V
  GND: Part1.GND, Part2.GND

custom parts:
  LIDAR-Lite: PulsedLight LIDAR-Lite Sensor
