# Fritzing sketch Schematic_robot (saved by Fritzing 0.9.4)
breadboards: 1

parts:
  Part1 = Arduino Mega ADK (Rev3)
  M1 = DC Motor
  M2 = DC Motor
  M3 = DC Motor
  M4 = DC Motor
  BAT1 = Battery Holders [package=lipo-1100mAh]
  BAT2 = Battery Holders [package=lipo-1100mAh]
  BAT3 = Battery Holders [package=lipo-1100mAh]
  Part2 = LIDAR-Lite
  Part3 = Bluetooth HC-05 Macho
  S2 = Round Pushbutton
  Part4 = Logic Level Converter
  S1 = H-Bridge with L298N
  J1 = Power Jack [package=power_jack_pth_lock]
  J2 = Basic Servo
  J3 = Basic Servo

nets:
  N1: Part1.D19/RX1, Part3.RXD
  N2: Part1.D18/TX1, Part3.TXD
  N3: Part1.D15/RX3, Part4.TX2_HV
  N4: Part1.D14/TX3, Part4.RX2_HV
  GND: Part1.GND, BAT1.-, BAT2.-, BAT3.-, Part2.GND, Part3.GND, Part4.GND, S1.GND, J1.GNDBREAK, J2.gnd, J3.gnd
  N5: Part1.D9_PWM, J2.pulse
  N6: Part1.D2_PWM, S1.ENB
  N7: Part1.D3_PWM, S1.ENA
  N8: Part1.D4_PWM, S1.IN1
  N9: Part1.D5_PWM, S1.IN2
  N10: Part1.D6_PWM, S1.IN3
  N11: Part1.D7_PWM, S1.IN4
  N12: M1.pin_1, M2.pin_1, S1.M2-01
  N13: M1.pin_2, M2.pin_2, S1.M2-02
  N14: M3.pin_1, M4.pin_1, S1.M1-02
  N15: M3.pin_2, M4.pin_2, S1.M1-01
  N16: BAT1.+, BAT2.+, BAT3.+, S2.leg0
  VCC: Part2.5V, Part3.VCC, Part4.HV, S1.5V, J2.vcc, J3.vcc
  12V: S2.leg1, S1.12V, J1.GND

custom parts:
  LIDAR-Lite: PulsedLight LIDAR-Lite Sensor
  H-Bridge with L298N: h-bridge
