# Fritzing sketch Schematic_servo (saved by Fritzing 0.9.4)

parts:
  Part1 = Arduino Mega ADK (Rev3)
  J1 = Basic Servo
  J2 = Basic Servo

nets:
  N1: Part1.D9_PWM, J1.pulse
  5V: Part1.5V, J1.vcc
  GND: Part1.GND, J1.gnd, J2.gnd
